# Fritzing sketch nixie-display (saved by Fritzing 0.9.4)
circuit board: 12.1615cm x 6.59cm

parts:
  NIXIE1 = IN-12 Nixie tube [part_number=IN-12B]
  K155ID2 = K155ID1 [package="DIP16 [THT]"]
  K155ID3 = K155ID1 [package="DIP16 [THT]"]
  NIXIE2 = IN-12 Nixie tube [part_number=IN-12B]
  NIXIE3 = IN-12 Nixie tube [part_number=IN-12B]
  NIXIE4 = IN-12 Nixie tube [part_number=IN-12B]
  R2 = Resistor [tolerance=±5% resistance=15k package=THT]
  R3 = Resistor [tolerance=±5% resistance=15k package=THT]
  R4 = Resistor [tolerance=±5% resistance=15k package=THT]
  K155ID1 = K155ID1 [package="DIP16 [THT]"]
  K155ID4 = K155ID1 [package="DIP16 [THT]"]
  J1 = screw terminal, 2 pins
  R1 = Resistor [tolerance=±5% resistance=15k package=THT]
  IO = double row male pin header, 8 pins [form="♂ (male)"]
  HV1 = NCH8200HV
  Mod1 = seeeduino-xiao
  U1 = 74HC595 [package="DIP16 [THT]"]
  U2 = 74HC595 [package="DIP16 [THT]"]
  INS-1 = LED - 5mm [color="White (4500K)" package="5 mm [THT]"]
  INS-1_2 = LED - 5mm [color="White (4500K)" package="5 mm [THT]"]
  R6 = Resistor [tolerance=±5% resistance=250k package=THT]
  Q1 = NPN-Transistor [part_number=MPSA42 package="TO92 [THT]"]
  R5 = Resistor [tolerance=±5% resistance=33k package=THT]
  ZS-042_RTC1 = ZS-042 RTC Module (fixed)
  C1 = Electrolytic Capacitor [capacitance=100µF voltage=10V package="100 mil [THT, electrolytic]"]
  C2 = Ceramic Capacitor [capacitance=100nF package="200 mil [THT, multilayer]"]
  C3 = Ceramic Capacitor [capacitance=100nF package="200 mil [THT, multilayer]"]
  C4 = Ceramic Capacitor [capacitance=100nF package="200 mil [THT, multilayer]"]
  C5 = Ceramic Capacitor [capacitance=100nF package="200 mil [THT, multilayer]"]
  Composant1 = ins-1 holder  # not connected
  NEOPIXEL = male pin header, 3 pins [form="♂ (male)"]
  R7 = Resistor [tolerance=±5% resistance=250k package=THT]
  D1 = Rectifier Diode [part_number=1N4148 package="300 mil [THT]"]
  RGB_SMD_LED1 = SMD RGB LED (WS2812B) [package=5050]
  RGB_SMD_LED2 = SMD RGB LED (WS2812B) [package=5050]
  RGB_SMD_LED3 = SMD RGB LED (WS2812B) [package=5050]
  RGB_SMD_LED4 = SMD RGB LED (WS2812B) [package=5050]

nets:
  N1: NIXIE1.Anode, R1.Pin_0
  N2: NIXIE1.Cathode_0, K155ID1.Output_0
  N3: NIXIE1.Cathode_1, K155ID1.Output_1
  N4: NIXIE1.Cathode_2, K155ID1.Output_2
  N5: NIXIE1.Cathode_3, K155ID1.Ouput_3
  N6: NIXIE1.Cathode_4, K155ID1.Output_4
  N7: NIXIE1.Cathode_5, K155ID1.Output_5
  N8: NIXIE1.Cathode_6, K155ID1.Output_6
  N9: NIXIE1.Cathode_7, K155ID1.Output_7
  N10: NIXIE1.Cathode_8, K155ID1.Output_8
  N11: NIXIE1.Cathode_9, K155ID1.Output_9
  N12: K155ID2.Output_8, NIXIE2.Cathode_8
  N13: K155ID2.Output_9, NIXIE2.Cathode_9
  N14: K155ID2.Input_A, U1.Q3
  N15: K155ID2.Input_D, U1.Q2
  5V: K155ID2.VCC, K155ID3.VCC, K155ID1.VCC, K155ID4.VCC, J1.pin1, HV1.VIN, U1.MR, U1.VCC, U2.MR, U2.VCC, ZS-042_RTC1.VCC, C1.+, C2.0, C3.0, C4.1, C5.1, NEOPIXEL.pin1, D1.anode, RGB_SMD_LED1.VDD, RGB_SMD_LED2.VDD, RGB_SMD_LED3.VDD, RGB_SMD_LED4.VDD
  N16: K155ID2.Input_B, U1.Q1
  N17: K155ID2.Input_C, U1.Q0
  N18: K155ID2.Output_2, NIXIE2.Cathode_2
  N19: K155ID2.Ouput_3, NIXIE2.Cathode_3
  N20: K155ID2.Output_7, NIXIE2.Cathode_7
  N21: K155ID2.Output_6, NIXIE2.Cathode_6
  GND: K155ID2.GND, K155ID3.GND, K155ID1.GND, K155ID4.GND, J1.pin2, IO.pin5, IO.pin6, IO.pin7, IO.pin8, HV1.GND, Mod1.GND, U1.GND, U1.OE, U2.GND, U2.OE, Q1.E, ZS-042_RTC1.GND, C1.-, C2.1, C3.1, C4.0, C5.0, NEOPIXEL.pin3, RGB_SMD_LED1.VSS, RGB_SMD_LED2.VSS, RGB_SMD_LED3.VSS, RGB_SMD_LED4.VSS
  N22: K155ID2.Output_4, NIXIE2.Cathode_4
  N23: K155ID2.Output_5, NIXIE2.Cathode_5
  N24: K155ID2.Output_1, NIXIE2.Cathode_1
  N25: K155ID2.Output_0, NIXIE2.Cathode_0
  N26: K155ID3.Output_8, NIXIE3.Cathode_8
  N27: K155ID3.Output_9, NIXIE3.Cathode_9
  N28: K155ID3.Input_A, U2.Q7
  N29: K155ID3.Input_D, U2.Q6
  N30: K155ID3.Input_B, U2.Q5
  N31: K155ID3.Input_C, U2.Q4
  N32: K155ID3.Output_2, NIXIE3.Cathode_2
  N33: K155ID3.Ouput_3, NIXIE3.Cathode_3
  N34: K155ID3.Output_7, NIXIE3.Cathode_7
  N35: K155ID3.Output_6, NIXIE3.Cathode_6
  N36: K155ID3.Output_4, NIXIE3.Cathode_4
  N37: K155ID3.Output_5, NIXIE3.Cathode_5
  N38: K155ID3.Output_1, NIXIE3.Cathode_1
  N39: K155ID3.Output_0, NIXIE3.Cathode_0
  N40: NIXIE2.Anode, R2.Pin_0
  N41: NIXIE3.Anode, R3.Pin_0
  N42: NIXIE4.Anode, R4.Pin_0
  N43: NIXIE4.Cathode_0, K155ID4.Output_0
  N44: NIXIE4.Cathode_1, K155ID4.Output_1
  N45: NIXIE4.Cathode_2, K155ID4.Output_2
  N46: NIXIE4.Cathode_3, K155ID4.Ouput_3
  N47: NIXIE4.Cathode_4, K155ID4.Output_4
  N48: NIXIE4.Cathode_5, K155ID4.Output_5
  N49: NIXIE4.Cathode_6, K155ID4.Output_6
  N50: NIXIE4.Cathode_7, K155ID4.Output_7
  N51: NIXIE4.Cathode_8, K155ID4.Output_8
  N52: NIXIE4.Cathode_9, K155ID4.Output_9
  N53: R2.Pin_1, R3.Pin_1, R4.Pin_1, R1.Pin_1, HV1.VOUT, INS-1.anode, INS-1_2.anode
  N54: K155ID1.Input_A, U1.Q7
  N55: K155ID1.Input_D, U1.Q6
  N56: K155ID1.Input_B, U1.Q5
  N57: K155ID1.Input_C, U1.Q4
  N58: K155ID4.Input_A, U2.Q3
  N59: K155ID4.Input_D, U2.Q2
  N60: K155ID4.Input_B, U2.Q1
  N61: K155ID4.Input_C, U2.Q0
  N62: IO.pin1, Mod1.D10
  N63: IO.pin2, Mod1.D9
  N64: IO.pin3, Mod1.D8
  N65: IO.pin4, Mod1.D7
  N66: Mod1.D0, R5.Pin_0
  N67: Mod1.D1, U1.ST_CP, U2.ST_CP
  N68: Mod1.D2, U1.SH_CP, U2.SH_CP
  N69: Mod1.D3, U1.DS
  N70: Mod1.D4, ZS-042_RTC1.SDA
  N71: Mod1.D5, ZS-042_RTC1.SCL
  N72: Mod1.D6, NEOPIXEL.pin2, RGB_SMD_LED1.DIN
  N73: Mod1.5V, D1.cathode
  N74: U1.Q7', U2.DS
  N75: INS-1.cathode, R7.Pin_1
  N76: INS-1_2.cathode, R6.Pin_1
  N77: R6.Pin_0, Q1.C, R7.Pin_0
  N78: Q1.B, R5.Pin_1
  N79: RGB_SMD_LED1.DOUT, RGB_SMD_LED2.DIN
  N80: RGB_SMD_LED2.DOUT, RGB_SMD_LED3.DIN
  N81: RGB_SMD_LED3.DOUT, RGB_SMD_LED4.DIN

notes:
  GND
  5V
  JLCJLCJLCJLC
  SCL
  SDA
  GND LED VCC
  IN GND
  StrangePlanet 2021
  VCC

custom parts:
  IN-12 Nixie tube: Russian IN-12 Nixie neon indicator tube
  K155ID1: Russian BDC Register (41141 Clone)
  seeeduino-xiao: Seeeduino XIAO processor board.
  ZS-042 RTC Module (fixed): This is the ZS-042 RTC module which uses the Maxim DS3231 real time clock IC. The module has a battery holder for a LIR2032 or CR2032. The module also includes an Atmel AT24C32 32K EEPROM for storing important information. The module can operate at 3V3 and 5V.
  SMD RGB LED (WS2812B): The WS2812B is an RGB LED with a WS2811 control IC built right into the LED. Its improvement over its WS2812 ancestor is the reduction to 4 pins (a single power supply instead of 2) and dropping the requirement for the external resistors. The manufacturer says it has a better reverse connect protection.
