# Fritzing sketch nixie-display_extension (saved by Fritzing 0.9.4)
circuit board: 6.25998cm x 6.59cm

parts:
  NIXIE3 = IN-12 Nixie tube [part_number=IN-12B]
  NIXIE4 = IN-12 Nixie tube [part_number=IN-12B]
  R3 = Resistor [tolerance=±5% resistance=15k package=THT]
  R4 = Resistor [tolerance=±5% resistance=15k package=THT]
  U2 = 74HC595 [package="DIP16 [THT]"]
  C4 = Ceramic Capacitor [capacitance=100nF package="200 mil [THT, multilayer]"]
  C3 = Ceramic Capacitor [capacitance=100nF package="200 mil [THT, multilayer]"]
  J1 = screw terminal, 3 pins
  K155ID3 = K155ID1 [package="DIP16 [THT]"]
  K155ID4 = K155ID1 [package="DIP16 [THT]"]
  RGB_SMD_LED5 = SMD RGB LED (WS2812B) [package=5050]
  RGB_SMD_LED6 = SMD RGB LED (WS2812B) [package=5050]
  J2 = male pin header, 4 pins [form="♂ (male)"]

nets:
  N1: NIXIE3.Anode, R3.Pin_0
  N2: NIXIE3.Cathode_0, K155ID3.Output_0
  N3: NIXIE3.Cathode_1, K155ID3.Output_1
  N4: NIXIE3.Cathode_2, K155ID3.Output_2
  N5: NIXIE3.Cathode_3, K155ID3.Ouput_3
  N6: NIXIE3.Cathode_4, K155ID3.Output_4
  N7: NIXIE3.Cathode_5, K155ID3.Output_5
  N8: NIXIE3.Cathode_6, K155ID3.Output_6
  N9: NIXIE3.Cathode_7, K155ID3.Output_7
  N10: NIXIE3.Cathode_8, K155ID3.Output_8
  N11: NIXIE3.Cathode_9, K155ID3.Output_9
  N12: NIXIE4.Anode, R4.Pin_0
  N13: NIXIE4.Cathode_0, K155ID4.Output_0
  N14: NIXIE4.Cathode_1, K155ID4.Output_1
  N15: NIXIE4.Cathode_2, K155ID4.Output_2
  N16: NIXIE4.Cathode_3, K155ID4.Ouput_3
  N17: NIXIE4.Cathode_4, K155ID4.Output_4
  N18: NIXIE4.Cathode_5, K155ID4.Output_5
  N19: NIXIE4.Cathode_6, K155ID4.Output_6
  N20: NIXIE4.Cathode_7, K155ID4.Output_7
  N21: NIXIE4.Cathode_8, K155ID4.Output_8
  N22: NIXIE4.Cathode_9, K155ID4.Output_9
  200V: R3.Pin_1, R4.Pin_1, J1.pin3
  N23: U2.Q1, K155ID4.Input_B
  N24: U2.Q2, K155ID4.Input_D
  N25: U2.Q3, K155ID4.Input_A
  N26: U2.Q4, K155ID3.Input_C
  N27: U2.Q5, K155ID3.Input_B
  N28: U2.Q6, K155ID3.Input_D
  N29: U2.Q7, K155ID3.Input_A
  GND: U2.GND, U2.OE, C4.0, C3.1, J1.pin2, K155ID3.GND, K155ID4.GND, RGB_SMD_LED5.VSS, RGB_SMD_LED6.VSS
  5V: U2.MR, U2.VCC, C4.1, C3.0, J1.pin1, K155ID3.VCC, K155ID4.VCC, RGB_SMD_LED5.VDD, RGB_SMD_LED6.VDD
  N30: U2.SH_CP, J2.pin2
  N31: U2.ST_CP, J2.pin3
  N32: U2.DS, J2.pin4
  N33: U2.Q0, K155ID4.Input_C
  N34: RGB_SMD_LED5.DOUT, RGB_SMD_LED6.DIN
  N35: RGB_SMD_LED5.DIN, J2.pin1

notes:
  GND
  5V
  JLCJLCJLCJLC
  StrangePlanet 2024
  LED SHCP STCP DS
  170V

custom parts:
  IN-12 Nixie tube: Russian IN-12 Nixie neon indicator tube
  K155ID1: Russian BDC Register (41141 Clone)
  SMD RGB LED (WS2812B): The WS2812B is an RGB LED with a WS2811 control IC built right into the LED. Its improvement over its WS2812 ancestor is the reduction to 4 pins (a single power supply instead of 2) and dropping the requirement for the external resistors. The manufacturer says it has a better reverse connect protection.
